# Fritzing sketch Circuit Pinout (saved by Fritzing 0.9.3b)

parts:
  M1 = DOIT Esp32 DevKit v1 (30 pins long, 11 pins width) [part_number=ESP32S-PIN30]
  8_Channel_Relay1 = 8 Channel Power Relay
  JACK1 = 2.1mm Barrel Jack with Terminal Block

nets:
  N1: M1.D2, 8_Channel_Relay1.IN8
  N2: M1.D18, 8_Channel_Relay1.IN5
  N3: M1.D19, 8_Channel_Relay1.IN4
  N4: M1.D21, 8_Channel_Relay1.IN3
  N5: M1.D22, 8_Channel_Relay1.IN2
  N6: M1.D23, 8_Channel_Relay1.IN1
  N7: M1.D12, 8_Channel_Relay1.IN7
  N8: M1.D13, 8_Channel_Relay1.IN6
  N9: 8_Channel_Relay1.GND, JACK1.NEG
  N10: 8_Channel_Relay1.VCC, 8_Channel_Relay1.JD-VCC, JACK1.POS

custom parts:
  DOIT Esp32 DevKit v1 (30 pins long, 11 pins width): The DOIT Esp32 DevKit v1 is one of the development board created by DOIT to evaluate the ESP-WROOM-32 module. It is based on the ESP32 microcontroller that boasts Wifi, Bluetooth, Ethernet and Low Power support all in a single chip. (vanepp) made breadboard work, adjusted pin numbering and labels and reduced size of schematic and cleaned up pcb. This chip is 30pins long (2 x15) and 11 pins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
  8 Channel Power Relay: An 8 channel power relay. The module operates at 5V.
